# Fritzing sketch Halloween2017PhysicalLayout (saved by Fritzing 0.9.3b)
breadboards: 1

parts:
  C1 = Tantalum Capacitor [capacitance=1μF package="100 mil [THT, tantalum]"]
  R1 = Resistor [tolerance=±5% resistance=220 package=THT]
  Part1 = Arduino Uno (Rev3) - ICSP
  R2 = Resistor [tolerance=±5% resistance=220 package=THT]
  R3 = Resistor [tolerance=±5% resistance=220 package=THT]
  J1 = Basic Servo
  IR1 = TSOP312.., 314.. [package=THT]
  LED1 = LED - 5mm [color="Red (633nm)" package="5 mm [THT]"]
  LED2 = smd LED [color="Red (633nm)" package="0805 [SMD]"]

nets:
  GND: C1.-, Part1.GND, J1.gnd, IR1.Vs, LED1.cathode, LED2.cathode
  N1: C1.+, R1.Pin_1, IR1.Data
  5V: R1.Pin_0, Part1.5V, J1.vcc
  N2: Part1.D8, IR1.GND
  N3: Part1.D3_PWM, J1.pulse
  N4: Part1.D5_PWM, R2.Pin_0
  N5: Part1.D6_PWM, R3.Pin_0
  N6: R2.Pin_1, LED1.anode
  N7: R3.Pin_1, LED2.anode
